// Digital circuit 8bit_adder.dig as structural Verilog
module _8bit_adder (
  input  [7:0] A,
  input  [7:0] B,
  input  Ci,
  output [7:0] S,
  output Ci_out
);

  wire CiA_out, CiB_out, CiC_out, CiD_out, CiE_out, CiF_out, CiG_out;

  // full_adder full_adder_1: pin names not known; wires that end beside it: A[7], B[7], CiG_out, S[7], Ci_out
  // full_adder full_adder_2: pin names not known; wires that end beside it: A[6], B[6], CiF_out, S[6], CiG_out
  // full_adder full_adder_3: pin names not known; wires that end beside it: A[5], B[5], CiE_out, S[5], CiF_out
  // full_adder full_adder_4: pin names not known; wires that end beside it: A[4], B[4], CiD_out, S[4], CiE_out
  // full_adder full_adder_5: pin names not known; wires that end beside it: A[3], B[3], CiC_out, S[3], CiD_out
  // full_adder full_adder_6: pin names not known; wires that end beside it: A[2], B[2], CiB_out, S[2], CiC_out
  // full_adder full_adder_7: pin names not known; wires that end beside it: A[1], B[1], CiA_out, S[1], CiB_out
  // full_adder full_adder_8: pin names not known; wires that end beside it: A[0], B[0], Ci, S[0], CiA_out
  // Pins of 1 and 8 bits meet at S

  // Other names for the same wires on the sheet: A00 = A[0]; A01 = A[1]; A02 = A[2]; A03 = A[3]; A04 = A[4];
  //   A05 = A[5]; A06 = A[6]; A07 = A[7]; B00 = B[0]; B01 = B[1]; B02 = B[2]; B03 = B[3]; B04 = B[4]; B05 = B[5];
  //   B06 = B[6]; B07 = B[7]; Ci_out_t = Ci; Co_out = Ci_out; S00 = S[0]; S_Out[7:0] = S; S01 = S[1]; S02 = S[2];
  //   S03 = S[3]; S04 = S[4]; S05 = S[5]; S06 = S[6]; S07 = S[7]
endmodule
