// Digital circuit 8bit_decrementor.dig as structural Verilog
module _8bit_decrementor (
  input  [7:0] A_in,
  output [7:0] S_out
);

  // _8bit_adder _8bit_adder_1: pin names not known; wires that end beside it: A_in, {8{1'b1}}, 1'b0, S_out
endmodule
