// Digital circuit 8bit_subtractor.dig as structural Verilog
module _8bit_subtractor (
  input  [7:0] A,
  input  [7:0] B,
  output [7:0] S
);

  wire [7:0] B_inv;

  assign B_inv = ~B;  // Not not_1, 8 bits wide
  // _8bit_adder _8bit_adder_1: pin names not known; wires that end beside it: A, B_inv, 1'b1, S
endmodule
