// Digital circuit adder_5bit.dig as structural Verilog
module adder_5bit (
  input  [4:0] A,
  input  [4:0] B,
  input  Ci,
  output [4:0] S,
  output Co
);

  wire full_adder_1_p5, full_adder_2_p5, full_adder_3_p5, full_adder_4_p5;

  // full_adder full_adder_1: pin names not known; wires that end beside it: A[0], B[0], Ci, S[0], full_adder_1_p5
  // full_adder full_adder_2: pin names not known; wires that end beside it: A[1], B[1], full_adder_1_p5, S[1], full_adder_2_p5
  // full_adder full_adder_3: pin names not known; wires that end beside it: A[2], B[2], full_adder_2_p5, S[2], full_adder_3_p5
  // full_adder full_adder_4: pin names not known; wires that end beside it: A[3], B[3], full_adder_3_p5, S[3], full_adder_4_p5
  // full_adder full_adder_5: pin names not known; wires that end beside it: A[4], B[4], full_adder_4_p5, S[4], Co

  // Other names for the same wires on the sheet: Ci_in = Ci; Ci_out = Co
endmodule
