// Digital circuit main_cpu.dig as structural Verilog
module main_cpu (
  input  RST,
  input  CLK
);

  wire CanW, decoder_1_out_0, decoder_1_out_1, decoder_1_out_2, decoder_1_out_3, decoder_1_out_4,
       decoder_1_out_5, decoder_1_out_6, decoder_1_out_7, is_JUMP, is_JUMPZ, JUMPZ_ok, OR_out, PC_LOAD,
       Shall_JUMP, T1, T2, T3, T4, T5, T6, W, Z_out;
  wire [3:0] C_out, IR_ULA, MAR_out, multiplexer_1_out;
  wire [7:0] IR, RegA_out, RegB_out, RES, ROM_out;

  or or_1 (OR_out, T1, T4);
  sequenciator sequenciator_1 (.CLK(CLK), .RST(RST), .T1(T1), .T2(T2), .T3(T3), .T4(T4), .T5(T5), .T6(T6));
  Comparator #(.Bits(4)) comparator_1 (.a(IR[7:4]), .b(4'b1001), .eq(is_JUMP));  // open: gt, lt
  and and_1 (JUMPZ_ok, is_JUMPZ, Z_out);
  or or_2 (Shall_JUMP, JUMPZ_ok, is_JUMP);
  Comparator #(.Bits(4)) comparator_2 (.a(IR[7:4]), .b(4'b1010), .eq(is_JUMPZ));  // open: gt, lt
  Multiplexer #(.Bits(4)) multiplexer_1 (.sel(T4), .in_0(C_out), .in_1(IR[3:0]), .out(multiplexer_1_out));
  and and_2 (PC_LOAD, T4, Shall_JUMP);
  Seven_Seg_Hex seven_seg_hex_1 (.d(RegA_out[7:4]), .dp(1'b0));
  PC pc_1 (.CLK(CLK), .RST(RST), .EN(T2), .Jump_addr(IR[3:0]), .LOAD(PC_LOAD), .C_OUT(C_out));
  Seven_Seg_Hex seven_seg_hex_2 (.d(RegA_out[3:0]), .dp(1'b0));
  Register #(.Bits(4)) MAR (.D(multiplexer_1_out), .C(CLK), .en(OR_out), .Q(MAR_out));
  Register #(.Bits(8)) Reg_A (.D(RES), .C(CLK), .en(W), .Q(RegA_out));
  Register #(.Bits(8)) Reg_B (.D(ROM_out), .C(CLK), .en(T5), .Q(RegB_out));
  Register #(.Bits(8)) u_IR (.D(ROM_out), .C(CLK), .en(T3), .Q(IR));
  ROM #(.AddrBits(4), .Bits(8)) rom_1 (.A(MAR_out), .sel(1'b1), .D(ROM_out));
  and and_3 (W, T6, CanW);
  Decoder #(.Selector_Bits(4)) decoder_1 (
    .sel(IR_ULA), .out_0(decoder_1_out_0), .out_1(decoder_1_out_1), .out_2(decoder_1_out_2),
    .out_3(decoder_1_out_3), .out_4(decoder_1_out_4), .out_5(decoder_1_out_5), .out_6(decoder_1_out_6),
    .out_7(decoder_1_out_7));  // open: out_8, out_9, out_10, out_11, out_12, out_13, out_14, out_15
  or or_3 (CanW, decoder_1_out_0, decoder_1_out_1, decoder_1_out_2, decoder_1_out_3, decoder_1_out_4, decoder_1_out_5, decoder_1_out_6, decoder_1_out_7);
  Register #(.Bits(4)) OpCode_Reg (.D(IR[7:4]), .C(CLK), .en(T5), .Q(IR_ULA));
  // ULA ula_1: pin names not known; wires that end beside it: RegA_out, RegB_out, IR_ULA, RES, Z_out

  // Other names for the same wires on the sheet: MUX1[3:0] = IR[3:0]; IR_op[3:0] = IR[7:4]

  // Notes on the sheet:
  //   CLK: Hz: 3
  //   contents of rom_1 (hex, n*v repeats v):
  //   2e,3d,f,5c,ff,7*0,4,3,2,5
endmodule
