// Digital circuit newCPU.dig as structural Verilog
module newCPU (
  input  CLK,
  input  RST
);

  wire CPU_CLK, HLT, IR_ld, is_NEG, MAR_ld, not_1_out, OpCode, OUT_ld, PC_en, PC_ld, PC_out, RegA_ld,
       RegB_ld, ULA_op, WBus_sel, Z_Flag;
  wire [6:0] OUT_reg;
  wire [7:0] ans, MEM_data, neg_1_out, W_bus;

  memory memory_1 (.WBus_in(W_bus), .MAR_LD(MAR_ld), .CLK(CPU_CLK), .RST(RST), .Data_Out(MEM_data));
  // ControlUnit controlunit_1: pin names not known; wires that end beside it: OpCode, Z_Flag, CPU_CLK, RST, WBus_sel, PC_en, PC_ld, MAR_ld, IR_ld, RegA_ld, RegB_ld, OUT_ld, ULA_op, HLT
  // ResettableRegister OUT_Reg: pin names not known; wires that end beside it: W_bus, CPU_CLK, OUT_ld, RST, {is_NEG, OUT_reg}
  // newPC newpc_1: pin names not known; wires that end beside it: W_bus, PC_en, PC_ld, CPU_CLK, RST, PC_out
  // DataPath datapath_1: pin names not known; wires that end beside it: W_bus, RegA_ld, RegB_ld, IR_ld, ULA_op, WBus_sel, CPU_CLK, RST, MEM_data, PC_out, W_bus, OpCode, Z_Flag
  not not_1 (not_1_out, HLT);
  and and_1 (CPU_CLK, not_1_out, CLK);
  Seven_Seg_Hex seven_seg_hex_1 (.d(ans[7:4]), .dp(1'b0));
  Neg #(.Bits(8)) neg_1 (.in({is_NEG, OUT_reg}), .out(neg_1_out));
  Seven_Seg_Hex seven_seg_hex_2 (.d(ans[3:0]), .dp(1'b0));
  LED led_1 (.in(is_NEG));
  Multiplexer #(.Bits(8)) multiplexer_1 (.sel(is_NEG), .in_0({is_NEG, OUT_reg}), .in_1(neg_1_out), .out(ans));

  // Other names for the same wires on the sheet: OUT_reg[7] = is_NEG

  // Notes on the sheet:
  //   CLK: Hz: 3
endmodule
